# Fritzing sketch pio_square_signal_out (saved by Fritzing 0.9.6b)
breadboards: 1

parts:
  Pico_H1 = Raspberry Pi Pico H
  Pico_H2 = Raspberry Pi Pico H

nets:
  N1: Pico_H1.VSYS, Pico_H2.VSYS
  GND: Pico_H1.GND, Pico_H2.GND
  N2: Pico_H1.SWDIO, Pico_H2.GP3
  N3: Pico_H1.SWCLK, Pico_H2.GP2
  N4: Pico_H1.GP1, Pico_H2.GP4
  N5: Pico_H1.GP0, Pico_H2.GP5

notes:
  Picoprobe
  Signal Output

custom parts:
  Raspberry Pi Pico H: Raspberry Pi Pico H. Based around the RP2040 microcontroller the Pico H is a low cost microcontroller device bringing Raspberry Pi quality, cost, and easy of use to the microcontroller space.
